# Fritzing sketch Schematic (saved by Fritzing 0.9.6b)
breadboards: 2

parts:
  Part1 = Arduino Uno (Rev3)
  R1 = Trimmer Potentiometer [maximum_resistance=10kΩ package=THT]
  S1 = Pushbutton [package="[SMD]"]
  S2 = Pushbutton [package="[THT]"]
  RE1 = Rotary Encoder [package=THT]
  Part2 = Digital FM Radio Receiver
  U2 = LCD-16X2 [package=lcd-16x2_noholes]
  R2 = Resistor [tolerance=±5% resistance=220 package="1206 [SMD]"]
  S3 = Pushbutton [package="[THT]"]
  C1 = Capacitor [package=cap-pth-small2]
  C2 = Capacitor [package=cap-pth-small2]

nets:
  N1: Part1.A1, RE1.EncoderPinB
  N2: Part1.A2, RE1.EncoderPinA
  N3: Part1.A4/SDA, Part2.SDIO
  N4: Part1.A5/SCL, Part2.SCLK
  N5: Part1.D8, S2.Pin_1, S2.Pin_2, C1.2
  N6: Part1.D9_PWM, S1.Pin_1, S1.Pin_2, C2.2
  N7: Part1.D11_PWM/MOSI, U2.E
  N8: Part1.D12/MISO, U2.RS
  GND: Part1.GND, R1.leg1, S1.Pin_3, S1.Pin_4, S2.Pin_3, S2.Pin_4, Part2.GND, U2.VSS, U2.R_W, U2.K, S3.Pin_3, S3.Pin_4, C1.1, C2.1
  N9: Part1.D2, Part2.!RST
  N10: Part1.D3_PWM, Part2.!SEN
  N11: Part1.D4, U2.DB6
  N12: Part1.D5_PWM, U2.DB5
  N13: Part1.D6_PWM, U2.DB4
  N14: Part1.D7, U2.DB7
  N15: Part1.RESET, S3.Pin_1, S3.Pin_2
  3V3: Part1.3V3, Part2.3.3V
  5V: Part1.5V, R1.leg2, RE1.EncoderPinC, U2.VDD, R2.Pin_0
  N16: R1.wiper, U2.VO
  N17: U2.A, R2.Pin_1
