# Fritzing sketch Schematic_nano (saved by Fritzing 0.9.6b)
circuit board: 7cm x 4.9cm

parts:
  Arduino = Arduino Nano (Rev3.0)
  Radio = Digital FM Radio Receiver
  Display = LCD-16X2 [package=lcd-16x2_noholes]
  R11 = Resistor [tolerance=±5% resistance=220 package=THT]  # not connected
  R12 = Trimmer Potentiometer [maximum_resistance=10kΩ package=THT]
  Frequency_selector1 = Rotary Encoder [package=THT]
  Volume3 = Pushbutton [package="[THT]"]
  Volume4 = Pushbutton [package="[THT]"]
  Reset = Pushbutton [package="[THT]"]
  Mute = Pushbutton [package="[THT]"]
  C5 = Capacitor [package=cap-pth-small2]
  C6 = Capacitor [package=cap-pth-small2]
  Mute_LED1 = LEDs [package=led10mm]  # not connected
  Rotary_Encoder_Button = Pushbutton [package="[THT]"]
  R13 = Resistor [tolerance=±5% resistance=220 package="1206 [SMD]"]
  Power_button3 = SWITCH-SPST-2 [package=switch-spst-vertical]  # not connected
  R14 = Resistor [tolerance=±5% resistance=220 package="2512 [SMD]"]

nets:
  N1: Arduino.RESET, Reset.Pin_1
  N2: Arduino.D2, Radio.!RST
  N3: Arduino.D3, Radio.!SEN
  N4: Arduino.D4, Display.DB4
  N5: Arduino.D5, Display.DB5
  N6: Arduino.D6, Display.DB6
  N7: Arduino.D7, Display.DB7
  N8: Arduino.D8, Volume3.Pin_1, Volume3.Pin_2, C5.2
  N9: Arduino.D9, Volume4.Pin_1, Volume4.Pin_2, C6.2
  N10: Arduino.D10, Mute.Pin_1, Mute.Pin_2
  N11: Arduino.D11/MOSI, Display.E
  N12: Arduino.D12/MISO, Display.RS
  GND: Arduino.GND, Radio.GND
  N13: Arduino.A5, Radio.SCLK
  N14: Arduino.A4, Radio.SDIO
  N15: Arduino.A3, R14.Pin_1
  N16: Arduino.A2, Frequency_selector1.EncoderPinA
  N17: Arduino.A1, Frequency_selector1.EncoderPinB
  N18: Arduino.A0, R13.Pin_1
  3V3: Arduino.3V3, Radio.3.3V
  N19: Arduino.D13/SCK, Rotary_Encoder_Button.Pin_1
  N20: Display.VO, R12.wiper
  N21: Volume3.Pin_3, Volume3.Pin_4, C5.1
  N22: Volume4.Pin_3, Volume4.Pin_4, C6.1
